// Logisim project Multiplicador_4Bits.circ as structural Verilog: 1 circuit, main circuit main
module main (
  input  in_1,
  input  in_2,
  input  in_3,
  input  in_4,
  input  in_5,
  input  in_6,
  input  in_7,
  input  in_8,
  output out_9,
  output out_10,
  output out_11,
  output out_12,
  output out_13,
  output out_14,
  output out_15,
  output out_16
);

  wire adder_1_cout, adder_1_out, adder_2_cout, adder_4_cout, adder_5_cout, adder_5_out, adder_6_cout,
       adder_6_out, adder_7_cout, adder_8_cout, adder_8_out, adder_9_cout, and_1_out, and_2_out, and_3_out,
       and_5_out, and_6_out, and_7_out, and_8_out, and_9_out, and_10_out, and_11_out, and_12_out, and_14_out,
       and_15_out, and_16_out;

  and and_1 (and_1_out, in_1, in_5);
  and and_2 (and_2_out, in_1, in_6);
  and and_3 (and_3_out, in_1, in_7);
  and and_4 (out_15, in_1, in_8);
  and and_5 (and_5_out, in_2, in_5);
  and and_6 (and_6_out, in_2, in_6);
  and and_7 (and_7_out, in_2, in_7);
  and and_8 (and_8_out, in_2, in_8);
  Adder #(.width(1)) adder_1 (.a(and_2_out), .b(and_7_out), .out(adder_1_out), .cin(adder_9_cout), .cout(adder_1_cout));
  and and_9 (and_9_out, in_3, in_5);
  and and_10 (and_10_out, in_3, in_6);
  and and_11 (and_11_out, in_3, in_7);
  and and_12 (and_12_out, in_3, in_8);
  Adder #(.width(1)) adder_2 (.a(adder_1_out), .b(and_12_out), .out(out_13), .cin(adder_1_cout), .cout(adder_2_cout));
  Adder #(.width(1)) adder_3 (.a(and_3_out), .b(and_8_out), .out(out_14), .cin(adder_2_cout), .cout(out_16));
  and and_13 (out_9, in_4, in_5);
  and and_14 (and_14_out, in_4, in_6);
  and and_15 (and_15_out, in_4, in_7);
  and and_16 (and_16_out, in_4, in_8);
  Adder #(.width(1)) adder_4 (.a(and_9_out), .b(and_14_out), .out(out_10), .cout(adder_4_cout));  // open: cin
  Adder #(.width(1)) adder_5 (
    .a(and_5_out), .b(and_10_out), .out(adder_5_out), .cin(adder_4_cout), .cout(adder_5_cout));
  Adder #(.width(1)) adder_6 (.a(and_1_out), .b(and_6_out), .out(adder_6_out), .cin(adder_7_cout), .cout(adder_6_cout));
  Adder #(.width(1)) adder_7 (.a(adder_5_out), .b(and_15_out), .out(out_11), .cin(adder_5_cout), .cout(adder_7_cout));
  Adder #(.width(1)) adder_8 (
    .a(adder_6_out), .b(and_11_out), .out(adder_8_out), .cin(adder_6_cout), .cout(adder_8_cout));
  Adder #(.width(1)) adder_9 (.a(adder_8_out), .b(and_16_out), .out(out_12), .cin(adder_8_cout), .cout(adder_9_cout));
endmodule
